// Logisim project project_2_14_6.circ as structural Verilog: 3 circuits, main circuit main
module main (
  input  d,
  output q,
  output notQ
);

  wire clk_out, not_1_out, not_2_out;

  Clock sysclk ();  // open: out
  Clock #(.highDuration(2), .lowDuration(2)) clk (.out(clk_out));
  not not_1 (not_1_out, clk_out);
  not not_2 (not_2_out, not_1_out);
endmodule

module DFlipFlop (
  input  D,
  input  Rst,
  output Q,
  output NotQ
);

  wire and_1_out, Clk_out, dlatch_1_q, not_1_out, not_2_out, not_3_out;

  Clock #(.highDuration(2), .lowDuration(2)) Clk (.out(Clk_out));
  Clock sysclk ();  // open: out
  not not_1 (not_1_out, Rst);
  not not_2 (not_2_out, Clk_out);
  and and_1 (and_1_out, D, not_1_out);
  not not_3 (not_3_out, not_2_out);
  DLatch dlatch_1 (.D(and_1_out), .Clk(not_2_out), .Q(dlatch_1_q));  // open: NotQ
  DLatch dlatch_2 (.D(dlatch_1_q), .Clk(not_3_out), .Q(Q), .NotQ(NotQ));
endmodule

module DLatch (
  input  D,
  input  Clk,
  output Q,
  output NotQ
);

  wire nand_1_out, nand_2_out, not_1_out;

  Clock sysclk ();  // open: out
  not not_1 (not_1_out, D);
  nand nand_1 (nand_1_out, D, Clk);
  nand nand_2 (nand_2_out, Clk, not_1_out);
  nand nand_3 (Q, nand_1_out, NotQ);
  nand nand_4 (NotQ, Q, nand_2_out);
endmodule
